// Logisim project 7seg.circ as structural Verilog: 1 circuit, main circuit main
module main (
  input  E0,
  input  E1,
  input  E2,
  input  E3,
  output out_5,
  output out_6,
  output out_7,
  output out_8,
  output out_9,
  output out_10,
  output out_11
);

  wire and_1_out, and_2_out, and_3_out, and_4_out, and_5_out, and_6_out, and_7_out, and_8_out, and_9_out,
       not_1_out, not_2_out, not_3_out, not_4_out, not_5_out, not_6_out;

  not not_1 (not_1_out, E1);
  not not_2 (not_2_out, E1);
  not not_3 (not_3_out, E0);
  not not_4 (not_4_out, E2);
  not not_5 (not_5_out, E0);
  not not_6 (not_6_out, E2);
  and and_1 (and_1_out, E0, not_2_out);
  and and_2 (and_2_out, not_5_out, E1);
  and and_3 (and_3_out, E1, not_6_out);
  and and_4 (and_4_out, not_2_out, not_6_out);
  and and_5 (and_5_out, E0, not_6_out);
  and and_6 (and_6_out, E0, E2);
  and and_7 (and_7_out, E1, E2);
  and and_8 (and_8_out, not_3_out, not_4_out);
  and and_9 (and_9_out, E2, and_1_out);
  or or_1 (out_5, E3, and_1_out, and_3_out, and_2_out);
  or or_2 (out_7, E3, and_1_out, and_5_out, and_4_out);
  or or_3 (out_6, E3, and_8_out, E1, and_6_out);
  or or_4 (out_8, E3, and_4_out, not_3_out, and_7_out);
  or or_5 (out_9, and_3_out, E3, and_8_out);
  or or_6 (out_10, and_2_out, and_8_out, E3, and_3_out, and_9_out);
  or or_7 (out_11, E3, E0, E2, not_1_out);

  // Notes on the sheet:
  //   E0E1'
  //   E0'E1
  //   E1E2'
  //   E1'E2'
  //   E0E2'
  //   E0E2
  //   E1E2
  //   E0'E2'
  //   E0E1'E2
  //   S1
  //   S2
  //   S3
  //   S4
  //   S5
  //   S6
  //   S7
endmodule
