// Logisim project ABCD.circ as structural Verilog: 1 circuit, main circuit main
module main (
  output LSB,
  output out_2,
  output out_3,
  output out_4,
  output MSB
);

  wire and_1_out, clock_1_out, j_k_ff_1_qn, j_k_ff_2_qn, j_k_ff_3_qn, j_k_ff_4_qn;

  Clock clock_1 (.out(clock_1_out));
  and and_1 (and_1_out, out_2, out_4);
  J_K_Flip_Flop j_k_ff_1 (
    .J(1'b1), .clk(clock_1_out), .K(1'b1), .Q(LSB), .Qn(j_k_ff_1_qn), .reset(and_1_out));  // open: preset, en
  J_K_Flip_Flop j_k_ff_2 (
    .J(1'b1), .clk(j_k_ff_1_qn), .K(1'b1), .Q(out_2), .Qn(j_k_ff_2_qn), .reset(and_1_out));  // open: preset, en
  J_K_Flip_Flop j_k_ff_3 (
    .J(1'b1), .clk(j_k_ff_2_qn), .K(1'b1), .Q(out_3), .Qn(j_k_ff_3_qn), .reset(and_1_out));  // open: preset, en
  J_K_Flip_Flop j_k_ff_4 (
    .J(1'b1), .clk(j_k_ff_3_qn), .K(1'b1), .Q(out_4), .Qn(j_k_ff_4_qn), .reset(and_1_out));  // open: preset, en
  J_K_Flip_Flop j_k_ff_5 (.J(1'b1), .clk(j_k_ff_4_qn), .K(1'b1), .Q(MSB), .reset(and_1_out));  // open: Qn, preset, en

  // Notes on the sheet:
  //   +Vcc(+5 V)
  //   Clock
  //   JK F/F 0
  //   Q0
  //   JK F/F 1
  //   Q1
  //   JK F/F 2
  //   Q2
  //   JK F/F 3
  //   Q3
  //   JK F/F 4
  //   Q4
endmodule
