// Logisim project abcd.circ as structural Verilog: 1 circuit, main circuit main
module main (
  input  Reset_input,
  output Q3,
  output Q2,
  output Q1,
  output Q0
);

  wire and_1_out, and_2_out, clock_1_out, d_ff_1_qn, d_ff_2_qn, d_ff_4_qn, n7_segment_display_driver_1_a_2,
       n7_segment_display_driver_1_b_2, n7_segment_display_driver_1_c_2, n7_segment_display_driver_1_d_2,
       n7_segment_display_driver_1_e, n7_segment_display_driver_1_f, n7_segment_display_driver_1_g, or_1_out;

  Clock clock_1 (.out(clock_1_out));
  and and_1 (and_1_out, d_ff_1_qn, d_ff_2_qn);
  D_Flip_Flop d_ff_1 (
    .clk(clock_1_out), .D(and_1_out), .Q(Q3), .Qn(d_ff_1_qn), .reset(Reset_input));  // open: preset, en
  or or_1 (or_1_out, Q3, Q0);
  D_Flip_Flop d_ff_2 (
    .clk(clock_1_out), .D(or_1_out), .Q(Q2), .Qn(d_ff_2_qn), .reset(Reset_input));  // open: preset, en
  and and_2 (and_2_out, Q2, d_ff_4_qn);
  D_Flip_Flop d_ff_3 (.clk(clock_1_out), .D(and_2_out), .Q(Q1), .reset(Reset_input));  // open: Qn, preset, en
  D_Flip_Flop d_ff_4 (.clk(clock_1_out), .D(Q3), .Q(Q0), .Qn(d_ff_4_qn), .reset(Reset_input));  // open: preset, en
  _7_segment_display_driver u_7_segment_display_driver_1 (
    .D(Q3), .C(Q2), .B(Q1), .A(Q0), .a_2(n7_segment_display_driver_1_a_2),
    .b_2(n7_segment_display_driver_1_b_2), .c_2(n7_segment_display_driver_1_c_2),
    .d_2(n7_segment_display_driver_1_d_2), .e(n7_segment_display_driver_1_e),
    .f(n7_segment_display_driver_1_f), .g(n7_segment_display_driver_1_g));
  _7_Segment_Display u_7_segment_display_1 (
    .g(n7_segment_display_driver_1_g), .f(n7_segment_display_driver_1_f),
    .a(n7_segment_display_driver_1_a_2), .b(n7_segment_display_driver_1_b_2),
    .e(n7_segment_display_driver_1_e), .d(n7_segment_display_driver_1_d_2),
    .c(n7_segment_display_driver_1_c_2));  // open: dp

  // Notes on the sheet:
  //   Clock
  //   D3
  //   q3'q2'
  //   q3+q0
  //   D2
  //   D1
  //   q2q0'
  //   q3
  //   D0
  //   7 seg Decoder
endmodule
