// Logisim project counter.circ as structural Verilog: 1 circuit, main circuit main
module main (
);

  wire and_1_out, and_2_out, clock_1_out, d_ff_1_q, d_ff_1_qn, d_ff_2_q, d_ff_2_qn, j_k_ff_1_q, or_1_out,
       or_2_out;

  Clock clock_1 (.out(clock_1_out));
  D_Flip_Flop d_ff_1 (.clk(clock_1_out), .D(d_ff_1_qn), .Q(d_ff_1_q), .Qn(d_ff_1_qn));  // open: preset, en, reset
  LED led_1 (.in(d_ff_1_q));
  or or_1 (or_1_out, d_ff_1_qn, d_ff_2_q);
  LED led_2 (.in(j_k_ff_1_q));
  J_K_Flip_Flop j_k_ff_1 (
    .J(d_ff_1_qn), .clk(clock_1_out), .K(or_1_out), .Q(j_k_ff_1_q));  // open: Qn, preset, en, reset
  and and_1 (and_1_out, d_ff_2_q, j_k_ff_1_q);
  and and_2 (and_2_out, d_ff_1_qn, d_ff_2_qn);
  D_Flip_Flop d_ff_2 (.clk(clock_1_out), .D(or_2_out), .Q(d_ff_2_q), .Qn(d_ff_2_qn));  // open: preset, en, reset
  or or_2 (or_2_out, and_1_out, and_2_out);
  LED led_3 (.in(d_ff_2_q));

  // Notes on the sheet:
  //   clock
  //   q2'
  //   D2 FF
  //   Q2
  //   q2'
  //   q0
  //   q1'
  //   Q1
  //   K1K1 FF
  //   qo+q2'
  //   q2'q0'+q1q0
  //   q1.q0
  //   q2'.q0'
  //   D0 FF
  //   Q0
endmodule
