// Logisim project muxxx.circ as structural Verilog: 1 circuit, main circuit main
module main (
  input  Bin,
  input  Y,
  input  X,
  output D,
  output Bout
);

  wire multiplexer_1_out, multiplexer_2_out, multiplexer_3_out, multiplexer_4_out, multiplexer_5_out,
       multiplexer_6_out, multiplexer_7_out, multiplexer_8_out, multiplexer_9_out, multiplexer_10_out,
       multiplexer_11_out, multiplexer_12_out, multiplexer_15_out, undriven, undriven_2, undriven_3;

  Multiplexer #(.enable("false")) multiplexer_1 (.in0(1'b0), .in1(1'b1), .out(multiplexer_1_out), .sel(Bin));
  Multiplexer #(.enable("false")) multiplexer_2 (.in0(1'b1), .in1(1'b0), .out(multiplexer_2_out), .sel(Bin));
  Multiplexer #(.enable("false")) multiplexer_3 (.in0(1'b1), .in1(1'b0), .out(multiplexer_3_out), .sel(Bin));
  Multiplexer #(.enable("false")) multiplexer_4 (.in0(1'b0), .in1(1'b1), .out(multiplexer_4_out), .sel(Bin));
  Multiplexer #(.enable("false")) multiplexer_5 (.in0(1'b0), .in1(1'b1), .out(multiplexer_5_out), .sel(Bin));
  Multiplexer #(.enable("false")) multiplexer_6 (.in0(1'b1), .in1(1'b1), .out(multiplexer_6_out), .sel(Bin));
  Multiplexer #(.enable("false")) multiplexer_7 (.in0(1'b0), .in1(1'b0), .out(multiplexer_7_out), .sel(Bin));
  Multiplexer #(.enable("false")) multiplexer_8 (.in0(1'b0), .in1(1'b1), .out(multiplexer_8_out), .sel(Bin));
  Multiplexer #(.enable("false")) multiplexer_9 (
    .in0(multiplexer_1_out), .in1(multiplexer_2_out), .out(multiplexer_9_out), .sel(Y));
  Multiplexer #(.enable("false")) multiplexer_10 (
    .in0(multiplexer_3_out), .in1(multiplexer_4_out), .out(multiplexer_10_out), .sel(Y));
  Multiplexer #(.enable("false")) multiplexer_11 (
    .in0(multiplexer_5_out), .in1(multiplexer_6_out), .out(multiplexer_11_out), .sel(Y));
  Multiplexer #(.enable("false")) multiplexer_12 (
    .in0(multiplexer_7_out), .in1(multiplexer_8_out), .out(multiplexer_12_out), .sel(Y));
  Multiplexer #(.enable("false")) multiplexer_13 (.in0(multiplexer_9_out), .in1(multiplexer_10_out), .out(D), .sel(X));
  Multiplexer #(.enable("false")) multiplexer_14 (
    .in0(multiplexer_11_out), .in1(multiplexer_12_out), .out(Bout), .sel(X));
  Multiplexer #(.enable("false")) multiplexer_15 (
    .in0(undriven), .in1(undriven_2), .out(multiplexer_15_out), .sel(undriven_3));

  // Notes on the sheet:
  //   +Vcc
  //   Ground
  //   D0
  //   D1
  //   Block diagram of 2:1 MUX
  //   S
  //   Y
endmodule
