// Logisim project trafic.circ as structural Verilog: 1 circuit, main circuit main
module main (
);

  wire and_1_out, and_2_out, and_3_out, and_4_out, clock_1_out, d_ff_1_q, d_ff_1_qn, d_ff_2_q, d_ff_2_qn;

  Clock clock_1 (.out(clock_1_out));
  D_Flip_Flop d_ff_1 (
    .clk(clock_1_out), .D(d_ff_1_qn), .Q(d_ff_1_q), .Qn(d_ff_1_qn), .reset(and_4_out));  // open: preset, en
  and and_1 (and_1_out, d_ff_1_qn, d_ff_2_qn);
  LED led_1 (.in(and_1_out));
  and and_2 (and_2_out, d_ff_1_q, d_ff_2_qn);
  LED led_2 (.in(and_2_out));
  D_Flip_Flop d_ff_2 (
    .clk(d_ff_1_qn), .D(d_ff_2_qn), .Q(d_ff_2_q), .Qn(d_ff_2_qn), .reset(and_4_out));  // open: preset, en
  and and_3 (and_3_out, d_ff_1_qn, d_ff_2_q);
  LED led_3 (.in(and_3_out));
  and and_4 (and_4_out, d_ff_2_q, d_ff_1_q);

  // Notes on the sheet:
  //   clock
  //   Q0
  //   Q1'.Q0'
  //   Green
  //   Q1'.Q0
  //   Yellow
  //   Q1
  //   Q1.Q0'
  //   Red
endmodule
